// Logisim project 3-bit Counter (FSMs).circ as structural Verilog: 1 circuit, main circuit main
module main (
  input  I,
  output N2,
  output N1,
  output N0
);

  wire and_1_out, and_2_out, and_3_out, and_4_out, and_5_out, and_6_out, and_7_out, and_8_out, and_9_out,
       clock_1_out, d_ff_1_q, d_ff_2_q, d_ff_3_q, not_1_out, not_2_out, not_3_out, not_4_out;

  not not_1 (not_1_out, I);
  not not_2 (not_2_out, d_ff_3_q);
  not not_3 (not_3_out, d_ff_2_q);
  not not_4 (not_4_out, d_ff_1_q);
  and and_1 (and_1_out, not_1_out, d_ff_1_q);
  and and_2 (and_2_out, d_ff_1_q, d_ff_2_q, not_2_out);
  and and_3 (and_3_out, d_ff_1_q, not_3_out);
  and and_4 (and_4_out, I, d_ff_3_q, not_3_out);
  and and_5 (and_5_out, not_2_out, d_ff_2_q);
  and and_6 (and_6_out, d_ff_2_q, not_1_out);
  and and_7 (and_7_out, I, not_2_out);
  and and_8 (and_8_out, not_1_out, d_ff_3_q);
  and and_9 (and_9_out, not_4_out, I, d_ff_2_q, d_ff_3_q);
  or or_1 (N0, and_7_out, and_8_out);
  or or_2 (N2, and_1_out, and_2_out, and_9_out, and_3_out);
  or or_3 (N1, and_4_out, and_5_out, and_6_out);
  Clock clock_1 (.out(clock_1_out));
  D_Flip_Flop d_ff_1 (.clk(clock_1_out), .D(N2), .Q(d_ff_1_q));  // open: Qn, preset, en, reset
  D_Flip_Flop d_ff_2 (.clk(clock_1_out), .D(N1), .Q(d_ff_2_q));  // open: Qn, preset, en, reset
  D_Flip_Flop d_ff_3 (.clk(clock_1_out), .D(N0), .Q(d_ff_3_q));  // open: Qn, preset, en, reset

  // Notes on the sheet:
  //   C2
  //   C1
  //   C0
endmodule
