// Logisim project AND(NAND) gate.circ as structural Verilog: 1 circuit, main circuit main
module main (
);

  wire nand_1_out, nand_2_out;

  nand nand_1 (nand_1_out, 1'b1, 1'b1);
  nand nand_2 (nand_2_out, nand_1_out, nand_1_out);
  // Probe on nand_2_out
endmodule
