// Logisim project Adder Chain.circ as structural Verilog: 1 circuit, main circuit main
module main (
);

  wire adder_1_cout, adder_1_out, adder_2_cout, adder_2_out, adder_3_cout, adder_3_out, adder_4_cout,
       adder_4_out;

  Adder #(.width(1)) adder_1 (.a(1'b1), .b(1'b1), .out(adder_1_out), .cin(1'b0), .cout(adder_1_cout));
  Adder #(.width(1)) adder_2 (.a(1'b1), .b(1'b1), .out(adder_2_out), .cin(adder_1_cout), .cout(adder_2_cout));
  Adder #(.width(1)) adder_3 (.a(1'b1), .b(1'b1), .out(adder_3_out), .cin(adder_2_cout), .cout(adder_3_cout));
  Adder #(.width(1)) adder_4 (.a(1'b1), .b(1'b1), .out(adder_4_out), .cin(adder_3_cout), .cout(adder_4_cout));
  // Probe on adder_4_cout
  // Probe on adder_1_out
  // Probe on adder_2_out
  // Probe on adder_3_out
  // Probe on adder_4_out
endmodule
