// Logisim project Adder-subtractor Chain.circ as structural Verilog: 1 circuit, main circuit main
module main (
  input  S,
  input  in_2,
  input  in_3,
  input  in_4,
  input  in_5,
  input  in_6,
  input  in_7,
  input  in_8,
  input  in_9
);

  wire adder_1_cout, adder_1_out, adder_2_cout, adder_2_out, adder_3_cout, adder_3_out, adder_4_cout,
       adder_4_out, multiplexer_1_out, multiplexer_2_out, multiplexer_3_out, multiplexer_4_out, not_1_out,
       not_2_out, not_3_out, not_4_out;

  Multiplexer multiplexer_1 (.in0(in_3), .in1(not_1_out), .out(multiplexer_1_out), .sel(S));  // open: en
  not not_1 (not_1_out, in_3);
  Multiplexer multiplexer_2 (.in0(in_5), .in1(not_2_out), .out(multiplexer_2_out), .sel(S));  // open: en
  not not_2 (not_2_out, in_5);
  Multiplexer multiplexer_3 (.in0(in_7), .in1(not_3_out), .out(multiplexer_3_out), .sel(S));  // open: en
  not not_3 (not_3_out, in_7);
  Multiplexer multiplexer_4 (.in0(in_9), .in1(not_4_out), .out(multiplexer_4_out), .sel(S));  // open: en
  not not_4 (not_4_out, in_9);
  Adder #(.width(1)) adder_1 (.a(in_2), .b(multiplexer_1_out), .out(adder_1_out), .cin(S), .cout(adder_1_cout));
  Adder #(.width(1)) adder_2 (
    .a(in_4), .b(multiplexer_2_out), .out(adder_2_out), .cin(adder_1_cout), .cout(adder_2_cout));
  Adder #(.width(1)) adder_3 (
    .a(in_6), .b(multiplexer_3_out), .out(adder_3_out), .cin(adder_2_cout), .cout(adder_3_cout));
  Adder #(.width(1)) adder_4 (
    .a(in_8), .b(multiplexer_4_out), .out(adder_4_out), .cin(adder_3_cout), .cout(adder_4_cout));
  // Probe on adder_4_cout
  // Probe on adder_1_out
  // Probe on adder_2_out
  // Probe on adder_3_out
  // Probe on adder_4_out
endmodule
