// Logisim project Inverter(Transister).circ as structural Verilog: 1 circuit, main circuit main
module main (
);

  wire transistor_1_out;

  Transistor transistor_1 (.in(1'b1), .out(transistor_1_out), .gate(1'b1));
  Transistor #(.\type ("n")) transistor_2 (.in(1'b0), .out(transistor_1_out), .gate(1'b1));
  // Probe on transistor_1_out
endmodule
