// Logisim project Multiplexer(NAND).circ as structural Verilog: 1 circuit, main circuit main
module main (
  input  A,
  input  S,
  input  B
);

  wire nand_1_out, nand_2_out, nand_3_out, nand_4_out;

  nand nand_1 (nand_1_out, S, S);
  nand nand_2 (nand_2_out, A, nand_1_out);
  nand nand_3 (nand_3_out, S, B);
  nand nand_4 (nand_4_out, nand_2_out, nand_3_out);
  // Probe on nand_4_out

  // Notes on the sheet:
  //   Q
endmodule
