// Logisim project NOT(NAMD) gate.circ as structural Verilog: 1 circuit, main circuit main
module main (
);

  wire nand_1_out;

  nand nand_1 (nand_1_out, 1'b1, 1'b1);
  // Probe on nand_1_out
endmodule
