// Logisim project SR-latch(NOR).circ as structural Verilog: 1 circuit, main circuit main
module main (
  input  in_1,
  input  R
);

  wire nor_1_out, nor_2_out;

  nor nor_1 (nor_1_out, in_1, nor_2_out);
  nor nor_2 (nor_2_out, nor_1_out, R);
  // Probe on nor_1_out
  // Probe on nor_2_out

  // Notes on the sheet:
  //   S
  //   D'
  //   D
endmodule
