// Logisim project Sequential logic.circ as structural Verilog: 1 circuit, main circuit main
module main (
  input  in_1,
  input  in_2,
  input  in_3
);

  wire adder_1_out, clock_1_out, d_ff_1_q, multiplexer_1_out;

  Multiplexer multiplexer_1 (.in0(d_ff_1_q), .in1(in_2), .out(multiplexer_1_out), .sel(in_1));  // open: en
  Adder #(.width(1)) adder_1 (.a(multiplexer_1_out), .b(in_3), .out(adder_1_out));  // open: cin, cout
  Clock clock_1 (.out(clock_1_out));
  D_Flip_Flop #(.trigger("falling")) d_ff_1 (
    .clk(clock_1_out), .D(adder_1_out), .Q(d_ff_1_q));  // open: Qn, preset, en, reset
endmodule
